# Fritzing sketch Wiring (saved by Fritzing 0.9.2b)
circuit board: 8.46667cm x 5.64444cm
breadboards: 1
perfboards: 1

parts:
  R1 = Resistor [tolerance=±5% resistance=4.7k package=THT]
  RHT1 = Humidity and Temperature Sensor RHT03
  Light_Sensor = Photocell (LDR) [package=THT]
  R2 = Resistor [tolerance=±5% resistance=4.7k package=THT]
  U1 = TEMPERATURE-SENSOR [package=to-92]
  U2 = TEMPERATURE-SENSOR [package=to-92]
  U3 = TEMPERATURE-SENSOR [package=to-92]
  R3 = Resistor [tolerance=±5% resistance=4.7k package=THT]
  Part1 = Arduino Yun

nets:
  VCC: R1.Pin_0, RHT1.Vcc, Light_Sensor.pin_0, R2.Pin_0, U1.VCC, U2.VCC, U3.VCC, R3.Pin_1, Part1.5V
  N1: R1.Pin_1, RHT1.Data-signal, Part1.D2/SDA, Part1.D2
  N2: RHT1.GND_2, U1.ADJ, U2.ADJ, U3.ADJ, Part1.GND
  N3: Light_Sensor.pin_1, R2.Pin_1, Part1.A0
  GND: U1.GND, U2.GND, U3.GND, R3.Pin_0, Part1.D10_PWM/SS
