# Fritzing sketch WiringBoard (saved by Fritzing 0.9.2b)
circuit board: 8.46667cm x 5.64444cm
perfboards: 2
breadboards: 1

parts:
  R1 = Resistor [tolerance=±5% resistance=4.7k package=THT]
  RHT1 = Humidity and Temperature Sensor RHT03
  Part1 = Arduino Yun
  Light_Sensor = Photocell (LDR) [package=THT]
  U1 = TEMPERATURE-SENSOR [package=to-92]
  U2 = TEMPERATURE-SENSOR [package=to-92]
  U3 = TEMPERATURE-SENSOR [package=to-92]
  R3 = Resistor [tolerance=±5% resistance=4.7k package=THT]
  R2 = Resistor [tolerance=±5% resistance=4.7k package=THT]
  R4 = Resistor [tolerance=±5% resistance=4.7k package=THT]  # not connected

nets:
  VCC: R1.Pin_0, RHT1.Vcc, Light_Sensor.pin_0, U1.VCC, U2.VCC, U3.VCC, R3.Pin_1, R2.Pin_0
  N1: R1.Pin_1, RHT1.Data-signal, Part1.D2
  N2: RHT1.GND_2, Part1.GND, U1.ADJ, U2.ADJ, U3.ADJ
  N3: Part1.A0, Light_Sensor.pin_1, R2.Pin_1
  GND: Part1.D10_PWM/SS, U1.GND, U2.GND, U3.GND, R3.Pin_0

notes:
  A4(SDA) A5(SCL):
  TWI - Reserved for Wire Library
  D0 (RX) D1(TX):
  USB Communication between Arduino and Linux
  D11(MOSI), D12 (MISO), D13(SCK) -
  SPI communication
